# Fritzing sketch Wifi Controller (saved by Fritzing 0.9.3b)
breadboards: 1

parts:
  Arduino_Uno_Wifi_Rev_2 = Arduino Uno (Rev3)
  U1 = JOYSTICK-PSP1000 [package=joystick-psp1000]
  4x_AA_Battery = Battery Holders [package=battery-aaa]
  On/Off_Switch = Toggle Switch [package=THT]
  Target_Device_Disconnected_Red_LED = LED - 5mm [color="Red (633nm)" package="5 mm [THT]"]
  Wifi_Disconnected_Red_LED = LED - 5mm [color="Red (633nm)" package="5 mm [THT]"]
  Wifi_Connected_Green_LED = LEDs [package=led10mm]
  Target_Device_Connected_Blue_LED = LEDs [package=led-1206]

nets:
  N1: Arduino_Uno_Wifi_Rev_2.A0, U1.X
  N2: Arduino_Uno_Wifi_Rev_2.A1, U1.Y
  GND: Arduino_Uno_Wifi_Rev_2.GND, U1.GND, On/Off_Switch.L2, Wifi_Disconnected_Red_LED.cathode, Wifi_Connected_Green_LED.C
  N3: Arduino_Uno_Wifi_Rev_2.D3_PWM, Target_Device_Disconnected_Red_LED.cathode, Wifi_Connected_Green_LED.A, Target_Device_Connected_Blue_LED.C
  N4: Arduino_Uno_Wifi_Rev_2.D4, Wifi_Disconnected_Red_LED.anode
  N5: Arduino_Uno_Wifi_Rev_2.D5_PWM, Target_Device_Connected_Blue_LED.A
  N6: Arduino_Uno_Wifi_Rev_2.D6_PWM, Target_Device_Disconnected_Red_LED.anode
  5V: Arduino_Uno_Wifi_Rev_2.5V, U1.VCC
  N7: Arduino_Uno_Wifi_Rev_2.VIN, 4x_AA_Battery.+
  N8: 4x_AA_Battery.-, On/Off_Switch.COM
